// Logisim project My 8 bit processor.circ as structural Verilog: 1 circuit, main circuit main
module main (
);

  wire and_1_out, and_2_out, and_3_out, and_4_out, and_9_out, and_10_out, and_11_out, and_12_out, and_17_out,
       and_18_out, and_19_out, and_20_out, and_25_out, and_26_out, and_27_out, and_28_out, and_33_out,
       and_34_out, and_35_out, and_36_out, and_41_out, and_42_out, and_43_out, and_44_out, and_49_out,
       and_50_out, and_51_out, and_52_out, and_57_out, and_58_out, and_59_out, and_60_out, and_65_out,
       and_66_out, and_67_out, and_68_out, and_73_out, and_74_out, and_75_out, and_76_out, and_81_out,
       and_82_out, and_83_out, and_84_out, and_89_out, and_90_out, and_91_out, and_92_out, and_97_out,
       and_98_out, and_99_out, and_100_out, and_105_out, and_106_out, and_107_out, and_108_out, and_113_out,
       and_114_out, and_115_out, and_116_out, and_121_out, and_122_out, and_123_out, and_124_out,
       and_129_out, and_130_out, and_131_out, and_132_out, and_137_out, and_138_out, and_139_out,
       and_140_out, and_145_out, and_146_out, and_147_out, and_148_out, and_153_out, and_154_out,
       and_155_out, and_156_out, and_161_out, and_162_out, and_163_out, and_164_out, and_169_out,
       and_170_out, and_171_out, and_172_out, and_177_out, and_178_out, and_179_out, and_180_out,
       and_185_out, and_186_out, and_187_out, and_188_out, and_193_out, and_194_out, and_195_out,
       and_196_out, and_201_out, and_202_out, and_203_out, and_204_out, and_209_out, and_210_out,
       and_211_out, and_212_out, and_217_out, and_218_out, and_219_out, and_220_out, and_225_out,
       and_226_out, and_227_out, and_228_out, and_233_out, and_234_out, and_235_out, and_236_out,
       and_241_out, and_242_out, and_243_out, and_244_out, and_249_out, and_250_out, and_251_out,
       and_252_out, button_1_out, d_ff_1_q, d_ff_2_q, d_ff_3_q, d_ff_4_q, d_ff_5_q, d_ff_6_q, d_ff_7_q,
       d_ff_8_q, d_ff_9_q, d_ff_10_q, d_ff_11_q, d_ff_12_q, d_ff_13_q, d_ff_14_q, d_ff_15_q, d_ff_16_q,
       d_ff_17_q, d_ff_18_q, d_ff_19_q, d_ff_20_q, d_ff_21_q, d_ff_22_q, d_ff_23_q, d_ff_24_q, d_ff_25_q,
       d_ff_26_q, d_ff_27_q, d_ff_28_q, d_ff_29_q, d_ff_30_q, d_ff_31_q, d_ff_32_q, d_ff_33_q, d_ff_34_q,
       d_ff_35_q, d_ff_36_q, d_ff_37_q, d_ff_38_q, d_ff_39_q, d_ff_40_q, d_ff_41_q, d_ff_42_q, d_ff_43_q,
       d_ff_44_q, d_ff_45_q, d_ff_46_q, d_ff_47_q, d_ff_48_q, d_ff_49_q, d_ff_50_q, d_ff_51_q, d_ff_52_q,
       d_ff_53_q, d_ff_54_q, d_ff_55_q, d_ff_56_q, d_ff_57_q, d_ff_58_q, d_ff_59_q, d_ff_60_q, d_ff_61_q,
       d_ff_62_q, d_ff_63_q, d_ff_64_q, d_ff_65_q, d_ff_66_q, d_ff_67_q, d_ff_68_q, d_ff_69_q, d_ff_70_q,
       d_ff_71_q, d_ff_72_q, d_ff_73_q, d_ff_74_q, d_ff_75_q, d_ff_76_q, d_ff_77_q, d_ff_78_q, d_ff_79_q,
       d_ff_80_q, d_ff_81_q, d_ff_82_q, d_ff_83_q, d_ff_84_q, d_ff_85_q, d_ff_86_q, d_ff_87_q, d_ff_88_q,
       d_ff_89_q, d_ff_90_q, d_ff_91_q, d_ff_92_q, d_ff_93_q, d_ff_94_q, d_ff_95_q, d_ff_96_q, d_ff_97_q,
       d_ff_98_q, d_ff_99_q, d_ff_100_q, d_ff_101_q, d_ff_102_q, d_ff_103_q, d_ff_104_q, d_ff_105_q,
       d_ff_106_q, d_ff_107_q, d_ff_108_q, d_ff_109_q, d_ff_110_q, d_ff_111_q, d_ff_112_q, d_ff_113_q,
       d_ff_114_q, d_ff_115_q, d_ff_116_q, d_ff_117_q, d_ff_118_q, d_ff_119_q, d_ff_120_q, d_ff_121_q,
       d_ff_122_q, d_ff_123_q, d_ff_124_q, d_ff_125_q, d_ff_126_q, d_ff_127_q, d_ff_128_q, decoder_1_out0,
       decoder_1_out1, decoder_1_out2, decoder_1_out3, decoder_2_out0, decoder_2_out2, decoder_2_out3,
       undriven;
  wire [7:0] register_1_q, register_2_q;
  wire [7:1] and_13_out, and_15_out;

  Button button_1 (.out(button_1_out));
  Decoder #(.select(4)) decoder_1 (
    .out0(decoder_1_out0), .out1(decoder_1_out1), .out2(decoder_1_out2), .out3(decoder_1_out3),
    .sel(register_2_q[7:4]), .en(1'b1));  // open: out4, out5, out6, out7, out8, out9, out10, out11, out12, out13, out14, out15
  Register register_1 (.Q(register_1_q));  // open: D, en, clk, clr
  Register register_2 (.Q(register_2_q));  // open: D, en, clk, clr
  Register register_3 (.D({and_13_out, and_13_out[4]}), .en(1'b1), .clk(undriven));  // open: Q, clr
  Button button_2 ();  // open: out
  Decoder #(.select(4)) decoder_2 (
    .out0(decoder_2_out0), .out1(and_13_out[7]), .out2(decoder_2_out2), .out3(decoder_2_out3),
    .sel(register_2_q[3:0]), .en(1'b1));  // open: out4, out5, out6, out7, out8, out9, out10, out11, out12, out13, out14, out15
  and and_1 (and_1_out, decoder_2_out0, decoder_1_out0, button_1_out);
  and and_2 (and_2_out, decoder_2_out0, decoder_1_out1, button_1_out);
  and and_3 (and_3_out, decoder_2_out0, decoder_1_out3, button_1_out);
  and and_4 (and_4_out, decoder_2_out0, decoder_1_out2, button_1_out);
  D_Flip_Flop d_ff_1 (.clk(and_1_out), .D(register_1_q[7]), .Q(d_ff_1_q), .en(1'b1));  // open: Qn, preset, reset
  D_Flip_Flop d_ff_2 (.clk(and_2_out), .D(register_1_q[7]), .Q(d_ff_2_q));  // open: Qn, preset, en, reset
  D_Flip_Flop d_ff_3 (.clk(and_3_out), .D(register_1_q[7]), .Q(d_ff_3_q));  // open: Qn, preset, en, reset
  D_Flip_Flop d_ff_4 (.clk(and_4_out), .D(register_1_q[7]), .Q(d_ff_4_q));  // open: Qn, preset, en, reset
  and and_5 (and_13_out[4], d_ff_1_q, decoder_1_out0, decoder_2_out0);
  and and_6 (and_13_out[4], d_ff_2_q, decoder_1_out1, decoder_2_out0);
  and and_7 (and_15_out[4], d_ff_3_q, decoder_1_out3, decoder_2_out0);
  and and_8 (and_15_out[4], d_ff_4_q, decoder_1_out2, decoder_2_out0);
  and and_9 (and_9_out, decoder_2_out0, decoder_1_out0, button_1_out);
  D_Flip_Flop d_ff_5 (.clk(and_9_out), .D(register_1_q[6]), .Q(d_ff_5_q));  // open: Qn, preset, en, reset
  and and_10 (and_10_out, decoder_2_out0, decoder_1_out1, button_1_out);
  D_Flip_Flop d_ff_6 (.clk(and_10_out), .D(register_1_q[6]), .Q(d_ff_6_q));  // open: Qn, preset, en, reset
  and and_11 (and_11_out, decoder_2_out0, decoder_1_out3, button_1_out);
  D_Flip_Flop d_ff_7 (.clk(and_11_out), .D(register_1_q[6]), .Q(d_ff_7_q));  // open: Qn, preset, en, reset
  and and_12 (and_12_out, decoder_2_out0, decoder_1_out2, button_1_out);
  D_Flip_Flop d_ff_8 (.clk(and_12_out), .D(register_1_q[6]), .Q(d_ff_8_q));  // open: Qn, preset, en, reset
  and and_13 (and_13_out[1], d_ff_5_q, decoder_1_out0, decoder_2_out0);
  and and_14 (and_13_out[1], d_ff_6_q, decoder_1_out1, decoder_2_out0);
  and and_15 (and_15_out[1], d_ff_7_q, decoder_1_out3, decoder_2_out0);
  and and_16 (and_15_out[1], d_ff_8_q, decoder_1_out2, decoder_2_out0);
  and and_17 (and_17_out, decoder_2_out0, decoder_1_out0, button_1_out);
  and and_18 (and_18_out, decoder_2_out0, decoder_1_out1, button_1_out);
  and and_19 (and_19_out, decoder_2_out0, decoder_1_out3, button_1_out);
  and and_20 (and_20_out, decoder_2_out0, decoder_1_out2, button_1_out);
  D_Flip_Flop d_ff_9 (.clk(and_17_out), .D(register_1_q[5]), .Q(d_ff_9_q));  // open: Qn, preset, en, reset
  and and_21 (and_13_out[2], d_ff_9_q, decoder_1_out0, decoder_2_out0);
  D_Flip_Flop d_ff_10 (.clk(and_18_out), .D(register_1_q[5]), .Q(d_ff_10_q));  // open: Qn, preset, en, reset
  and and_22 (and_13_out[2], d_ff_10_q, decoder_1_out1, decoder_2_out0);
  D_Flip_Flop d_ff_11 (.clk(and_19_out), .D(register_1_q[5]), .Q(d_ff_11_q));  // open: Qn, preset, en, reset
  and and_23 (and_15_out[2], d_ff_11_q, decoder_1_out3, decoder_2_out0);
  D_Flip_Flop d_ff_12 (.clk(and_20_out), .D(register_1_q[5]), .Q(d_ff_12_q));  // open: Qn, preset, en, reset
  and and_24 (and_15_out[2], d_ff_12_q, decoder_1_out2, decoder_2_out0);
  and and_25 (and_25_out, decoder_2_out0, decoder_1_out0, button_1_out);
  and and_26 (and_26_out, decoder_2_out0, decoder_1_out1, button_1_out);
  and and_27 (and_27_out, decoder_2_out0, decoder_1_out3, button_1_out);
  and and_28 (and_28_out, decoder_2_out0, decoder_1_out2, button_1_out);
  D_Flip_Flop d_ff_13 (.clk(and_25_out), .D(register_1_q[4]), .Q(d_ff_13_q));  // open: Qn, preset, en, reset
  D_Flip_Flop d_ff_14 (.clk(and_26_out), .D(register_1_q[4]), .Q(d_ff_14_q));  // open: Qn, preset, en, reset
  D_Flip_Flop d_ff_15 (.clk(and_27_out), .D(register_1_q[4]), .Q(d_ff_15_q));  // open: Qn, preset, en, reset
  D_Flip_Flop d_ff_16 (.clk(and_28_out), .D(register_1_q[4]), .Q(d_ff_16_q));  // open: Qn, preset, en, reset
  and and_29 (and_13_out[3], d_ff_13_q, decoder_1_out0, decoder_2_out0);
  and and_30 (and_13_out[3], d_ff_14_q, decoder_1_out1, decoder_2_out0);
  and and_31 (and_15_out[3], d_ff_15_q, decoder_1_out3, decoder_2_out0);
  and and_32 (and_15_out[3], d_ff_16_q, decoder_1_out2, decoder_2_out0);
  and and_33 (and_33_out, decoder_2_out0, decoder_1_out0, button_1_out);
  and and_34 (and_34_out, decoder_2_out0, decoder_1_out1, button_1_out);
  and and_35 (and_35_out, decoder_2_out0, decoder_1_out3, button_1_out);
  and and_36 (and_36_out, decoder_2_out0, decoder_1_out2, button_1_out);
  D_Flip_Flop d_ff_17 (.clk(and_33_out), .D(register_1_q[3]), .Q(d_ff_17_q));  // open: Qn, preset, en, reset
  D_Flip_Flop d_ff_18 (.clk(and_34_out), .D(register_1_q[3]), .Q(d_ff_18_q));  // open: Qn, preset, en, reset
  D_Flip_Flop d_ff_19 (.clk(and_35_out), .D(register_1_q[3]), .Q(d_ff_19_q));  // open: Qn, preset, en, reset
  D_Flip_Flop d_ff_20 (.clk(and_36_out), .D(register_1_q[3]), .Q(d_ff_20_q));  // open: Qn, preset, en, reset
  and and_37 (and_13_out[4], d_ff_17_q, decoder_1_out0, decoder_2_out0);
  and and_38 (and_13_out[4], d_ff_18_q, decoder_1_out1, decoder_2_out0);
  and and_39 (and_15_out[4], d_ff_19_q, decoder_1_out3, decoder_2_out0);
  and and_40 (and_15_out[4], d_ff_20_q, decoder_1_out2, decoder_2_out0);
  and and_41 (and_41_out, decoder_2_out0, decoder_1_out0, button_1_out);
  and and_42 (and_42_out, decoder_2_out0, decoder_1_out1, button_1_out);
  and and_43 (and_43_out, decoder_2_out0, decoder_1_out3, button_1_out);
  and and_44 (and_44_out, decoder_2_out0, decoder_1_out2, button_1_out);
  D_Flip_Flop d_ff_21 (.clk(and_41_out), .D(register_1_q[2]), .Q(d_ff_21_q));  // open: Qn, preset, en, reset
  D_Flip_Flop d_ff_22 (.clk(and_42_out), .D(register_1_q[2]), .Q(d_ff_22_q));  // open: Qn, preset, en, reset
  D_Flip_Flop d_ff_23 (.clk(and_43_out), .D(register_1_q[2]), .Q(d_ff_23_q));  // open: Qn, preset, en, reset
  D_Flip_Flop d_ff_24 (.clk(and_44_out), .D(register_1_q[2]), .Q(d_ff_24_q));  // open: Qn, preset, en, reset
  and and_45 (and_13_out[5], d_ff_21_q, decoder_1_out0, decoder_2_out0);
  and and_46 (and_13_out[5], d_ff_22_q, decoder_1_out1, decoder_2_out0);
  and and_47 (and_15_out[5], d_ff_23_q, decoder_1_out3, decoder_2_out0);
  and and_48 (and_15_out[5], d_ff_24_q, decoder_1_out2, decoder_2_out0);
  and and_49 (and_49_out, decoder_2_out0, decoder_1_out0, button_1_out);
  and and_50 (and_50_out, decoder_2_out0, decoder_1_out1, button_1_out);
  and and_51 (and_51_out, decoder_2_out0, decoder_1_out3, button_1_out);
  and and_52 (and_52_out, decoder_2_out0, decoder_1_out2, button_1_out);
  D_Flip_Flop d_ff_25 (.clk(and_49_out), .D(register_1_q[1]), .Q(d_ff_25_q));  // open: Qn, preset, en, reset
  D_Flip_Flop d_ff_26 (.clk(and_50_out), .D(register_1_q[1]), .Q(d_ff_26_q));  // open: Qn, preset, en, reset
  D_Flip_Flop d_ff_27 (.clk(and_51_out), .D(register_1_q[1]), .Q(d_ff_27_q));  // open: Qn, preset, en, reset
  D_Flip_Flop d_ff_28 (.clk(and_52_out), .D(register_1_q[1]), .Q(d_ff_28_q));  // open: Qn, preset, en, reset
  and and_53 (and_13_out[6], d_ff_25_q, decoder_1_out0, decoder_2_out0);
  and and_54 (and_13_out[6], d_ff_26_q, decoder_1_out1, decoder_2_out0);
  and and_55 (and_15_out[6], d_ff_27_q, decoder_1_out3, decoder_2_out0);
  and and_56 (and_15_out[6], d_ff_28_q, decoder_1_out2, decoder_2_out0);
  and and_57 (and_57_out, decoder_2_out0, decoder_1_out0, button_1_out);
  and and_58 (and_58_out, decoder_2_out0, decoder_1_out1, button_1_out);
  and and_59 (and_59_out, decoder_2_out0, decoder_1_out3, button_1_out);
  and and_60 (and_60_out, decoder_2_out0, decoder_1_out2, button_1_out);
  D_Flip_Flop d_ff_29 (.clk(and_57_out), .D(register_1_q[0]), .Q(d_ff_29_q));  // open: Qn, preset, en, reset
  D_Flip_Flop d_ff_30 (.clk(and_58_out), .D(register_1_q[0]), .Q(d_ff_30_q));  // open: Qn, preset, en, reset
  D_Flip_Flop d_ff_31 (.clk(and_59_out), .D(register_1_q[0]), .Q(d_ff_31_q));  // open: Qn, preset, en, reset
  D_Flip_Flop d_ff_32 (.clk(and_60_out), .D(register_1_q[0]), .Q(d_ff_32_q));  // open: Qn, preset, en, reset
  and and_61 (and_13_out[7], d_ff_29_q, decoder_1_out0, decoder_2_out0);
  and and_62 (and_13_out[7], d_ff_30_q, decoder_1_out1, decoder_2_out0);
  and and_63 (and_15_out[7], d_ff_31_q, decoder_1_out3, decoder_2_out0);
  and and_64 (and_15_out[7], d_ff_32_q, decoder_1_out2, decoder_2_out0);
  D_Flip_Flop d_ff_33 (.clk(and_65_out), .D(register_1_q[7]), .Q(d_ff_33_q));  // open: Qn, preset, en, reset
  and and_65 (and_65_out, and_13_out[7], decoder_1_out0, button_1_out);
  and and_66 (and_66_out, and_13_out[7], decoder_1_out1, button_1_out);
  D_Flip_Flop d_ff_34 (.clk(and_66_out), .D(register_1_q[7]), .Q(d_ff_34_q));  // open: Qn, preset, en, reset
  D_Flip_Flop d_ff_35 (.clk(and_67_out), .D(register_1_q[7]), .Q(d_ff_35_q));  // open: Qn, preset, en, reset
  and and_67 (and_67_out, and_13_out[7], decoder_1_out3, button_1_out);
  and and_68 (and_68_out, and_13_out[7], decoder_1_out2, button_1_out);
  D_Flip_Flop d_ff_36 (.clk(and_68_out), .D(register_1_q[7]), .Q(d_ff_36_q));  // open: Qn, preset, en, reset
  and and_69 (and_13_out[4], d_ff_33_q, decoder_1_out0, and_13_out[7]);
  and and_70 (and_13_out[4], d_ff_34_q, decoder_1_out1, and_13_out[7]);
  and and_71 (and_15_out[4], d_ff_35_q, decoder_1_out3, and_13_out[7]);
  and and_72 (and_15_out[4], d_ff_36_q, decoder_1_out2, and_13_out[7]);
  and and_73 (and_73_out, and_13_out[7], decoder_1_out0, button_1_out);
  and and_74 (and_74_out, and_13_out[7], decoder_1_out1, button_1_out);
  and and_75 (and_75_out, and_13_out[7], decoder_1_out3, button_1_out);
  and and_76 (and_76_out, and_13_out[7], decoder_1_out2, button_1_out);
  D_Flip_Flop d_ff_37 (.clk(and_73_out), .D(register_1_q[6]), .Q(d_ff_37_q));  // open: Qn, preset, en, reset
  and and_77 (and_13_out[1], d_ff_37_q, decoder_1_out0, and_13_out[7]);
  D_Flip_Flop d_ff_38 (.clk(and_74_out), .D(register_1_q[6]), .Q(d_ff_38_q));  // open: Qn, preset, en, reset
  and and_78 (and_13_out[1], d_ff_38_q, decoder_1_out1, and_13_out[7]);
  D_Flip_Flop d_ff_39 (.clk(and_75_out), .D(register_1_q[6]), .Q(d_ff_39_q));  // open: Qn, preset, en, reset
  and and_79 (and_15_out[1], d_ff_39_q, decoder_1_out3, and_13_out[7]);
  D_Flip_Flop d_ff_40 (.clk(and_76_out), .D(register_1_q[6]), .Q(d_ff_40_q));  // open: Qn, preset, en, reset
  and and_80 (and_15_out[1], d_ff_40_q, decoder_1_out2, and_13_out[7]);
  and and_81 (and_81_out, and_13_out[7], decoder_1_out0, button_1_out);
  and and_82 (and_82_out, and_13_out[7], decoder_1_out1, button_1_out);
  and and_83 (and_83_out, and_13_out[7], decoder_1_out3, button_1_out);
  and and_84 (and_84_out, and_13_out[7], decoder_1_out2, button_1_out);
  D_Flip_Flop d_ff_41 (.clk(and_81_out), .D(register_1_q[5]), .Q(d_ff_41_q));  // open: Qn, preset, en, reset
  D_Flip_Flop d_ff_42 (.clk(and_82_out), .D(register_1_q[5]), .Q(d_ff_42_q));  // open: Qn, preset, en, reset
  D_Flip_Flop d_ff_43 (.clk(and_83_out), .D(register_1_q[5]), .Q(d_ff_43_q));  // open: Qn, preset, en, reset
  D_Flip_Flop d_ff_44 (.clk(and_84_out), .D(register_1_q[5]), .Q(d_ff_44_q));  // open: Qn, preset, en, reset
  and and_85 (and_13_out[2], d_ff_41_q, decoder_1_out0, and_13_out[7]);
  and and_86 (and_13_out[2], d_ff_42_q, decoder_1_out1, and_13_out[7]);
  and and_87 (and_15_out[2], d_ff_43_q, decoder_1_out3, and_13_out[7]);
  and and_88 (and_15_out[2], d_ff_44_q, decoder_1_out2, and_13_out[7]);
  and and_89 (and_89_out, and_13_out[7], decoder_1_out0, button_1_out);
  and and_90 (and_90_out, and_13_out[7], decoder_1_out1, button_1_out);
  and and_91 (and_91_out, and_13_out[7], decoder_1_out3, button_1_out);
  and and_92 (and_92_out, and_13_out[7], decoder_1_out2, button_1_out);
  D_Flip_Flop d_ff_45 (.clk(and_89_out), .D(register_1_q[4]), .Q(d_ff_45_q));  // open: Qn, preset, en, reset
  D_Flip_Flop d_ff_46 (.clk(and_90_out), .D(register_1_q[4]), .Q(d_ff_46_q));  // open: Qn, preset, en, reset
  D_Flip_Flop d_ff_47 (.clk(and_91_out), .D(register_1_q[4]), .Q(d_ff_47_q));  // open: Qn, preset, en, reset
  D_Flip_Flop d_ff_48 (.clk(and_92_out), .D(register_1_q[4]), .Q(d_ff_48_q));  // open: Qn, preset, en, reset
  and and_93 (and_13_out[3], d_ff_45_q, decoder_1_out0, and_13_out[7]);
  and and_94 (and_13_out[3], d_ff_46_q, decoder_1_out1, and_13_out[7]);
  and and_95 (and_15_out[3], d_ff_47_q, decoder_1_out3, and_13_out[7]);
  and and_96 (and_15_out[3], d_ff_48_q, decoder_1_out2, and_13_out[7]);
  and and_97 (and_97_out, and_13_out[7], decoder_1_out0, button_1_out);
  and and_98 (and_98_out, and_13_out[7], decoder_1_out1, button_1_out);
  and and_99 (and_99_out, and_13_out[7], decoder_1_out3, button_1_out);
  and and_100 (and_100_out, and_13_out[7], decoder_1_out2, button_1_out);
  D_Flip_Flop d_ff_49 (.clk(and_97_out), .D(register_1_q[3]), .Q(d_ff_49_q));  // open: Qn, preset, en, reset
  D_Flip_Flop d_ff_50 (.clk(and_98_out), .D(register_1_q[3]), .Q(d_ff_50_q));  // open: Qn, preset, en, reset
  D_Flip_Flop d_ff_51 (.clk(and_99_out), .D(register_1_q[3]), .Q(d_ff_51_q));  // open: Qn, preset, en, reset
  D_Flip_Flop d_ff_52 (.clk(and_100_out), .D(register_1_q[3]), .Q(d_ff_52_q));  // open: Qn, preset, en, reset
  and and_101 (and_13_out[4], d_ff_49_q, decoder_1_out0, and_13_out[7]);
  and and_102 (and_13_out[4], d_ff_50_q, decoder_1_out1, and_13_out[7]);
  and and_103 (and_15_out[4], d_ff_51_q, decoder_1_out3, and_13_out[7]);
  and and_104 (and_15_out[4], d_ff_52_q, decoder_1_out2, and_13_out[7]);
  and and_105 (and_105_out, and_13_out[7], decoder_1_out0, button_1_out);
  and and_106 (and_106_out, and_13_out[7], decoder_1_out1, button_1_out);
  and and_107 (and_107_out, and_13_out[7], decoder_1_out3, button_1_out);
  and and_108 (and_108_out, and_13_out[7], decoder_1_out2, button_1_out);
  D_Flip_Flop d_ff_53 (.clk(and_105_out), .D(register_1_q[2]), .Q(d_ff_53_q));  // open: Qn, preset, en, reset
  D_Flip_Flop d_ff_54 (.clk(and_106_out), .D(register_1_q[2]), .Q(d_ff_54_q));  // open: Qn, preset, en, reset
  D_Flip_Flop d_ff_55 (.clk(and_107_out), .D(register_1_q[2]), .Q(d_ff_55_q));  // open: Qn, preset, en, reset
  D_Flip_Flop d_ff_56 (.clk(and_108_out), .D(register_1_q[2]), .Q(d_ff_56_q));  // open: Qn, preset, en, reset
  and and_109 (and_13_out[5], d_ff_53_q, decoder_1_out0, and_13_out[7]);
  and and_110 (and_13_out[5], d_ff_54_q, decoder_1_out1, and_13_out[7]);
  and and_111 (and_15_out[5], d_ff_55_q, decoder_1_out3, and_13_out[7]);
  and and_112 (and_15_out[5], d_ff_56_q, decoder_1_out2, and_13_out[7]);
  and and_113 (and_113_out, and_13_out[7], decoder_1_out0, button_1_out);
  and and_114 (and_114_out, and_13_out[7], decoder_1_out1, button_1_out);
  and and_115 (and_115_out, and_13_out[7], decoder_1_out3, button_1_out);
  and and_116 (and_116_out, and_13_out[7], decoder_1_out2, button_1_out);
  D_Flip_Flop d_ff_57 (.clk(and_113_out), .D(register_1_q[1]), .Q(d_ff_57_q));  // open: Qn, preset, en, reset
  D_Flip_Flop d_ff_58 (.clk(and_114_out), .D(register_1_q[1]), .Q(d_ff_58_q));  // open: Qn, preset, en, reset
  D_Flip_Flop d_ff_59 (.clk(and_115_out), .D(register_1_q[1]), .Q(d_ff_59_q));  // open: Qn, preset, en, reset
  D_Flip_Flop d_ff_60 (.clk(and_116_out), .D(register_1_q[1]), .Q(d_ff_60_q));  // open: Qn, preset, en, reset
  and and_117 (and_13_out[6], d_ff_57_q, decoder_1_out0, and_13_out[7]);
  and and_118 (and_13_out[6], d_ff_58_q, decoder_1_out1, and_13_out[7]);
  and and_119 (and_15_out[6], d_ff_59_q, decoder_1_out3, and_13_out[7]);
  and and_120 (and_15_out[6], d_ff_60_q, decoder_1_out2, and_13_out[7]);
  and and_121 (and_121_out, and_13_out[7], decoder_1_out0, button_1_out);
  and and_122 (and_122_out, and_13_out[7], decoder_1_out1, button_1_out);
  and and_123 (and_123_out, and_13_out[7], decoder_1_out3, button_1_out);
  and and_124 (and_124_out, and_13_out[7], decoder_1_out2, button_1_out);
  D_Flip_Flop d_ff_61 (.clk(and_121_out), .D(register_1_q[0]), .Q(d_ff_61_q));  // open: Qn, preset, en, reset
  D_Flip_Flop d_ff_62 (.clk(and_122_out), .D(register_1_q[0]), .Q(d_ff_62_q));  // open: Qn, preset, en, reset
  D_Flip_Flop d_ff_63 (.clk(and_123_out), .D(register_1_q[0]), .Q(d_ff_63_q));  // open: Qn, preset, en, reset
  D_Flip_Flop d_ff_64 (.clk(and_124_out), .D(register_1_q[0]), .Q(d_ff_64_q));  // open: Qn, preset, en, reset
  and and_125 (and_13_out[7], d_ff_61_q, decoder_1_out0, and_13_out[7]);
  and and_126 (and_13_out[7], d_ff_62_q, decoder_1_out1, and_13_out[7]);
  and and_127 (and_15_out[7], d_ff_63_q, decoder_1_out3, and_13_out[7]);
  and and_128 (and_15_out[7], d_ff_64_q, decoder_1_out2, and_13_out[7]);
  and and_129 (and_129_out, decoder_2_out2, decoder_1_out0, button_1_out);
  D_Flip_Flop d_ff_65 (.clk(and_129_out), .D(register_1_q[7]), .Q(d_ff_65_q));  // open: Qn, preset, en, reset
  D_Flip_Flop d_ff_66 (.clk(and_130_out), .D(register_1_q[7]), .Q(d_ff_66_q));  // open: Qn, preset, en, reset
  and and_130 (and_130_out, decoder_2_out2, decoder_1_out1, button_1_out);
  D_Flip_Flop d_ff_67 (.clk(and_131_out), .D(register_1_q[7]), .Q(d_ff_67_q));  // open: Qn, preset, en, reset
  and and_131 (and_131_out, decoder_2_out2, decoder_1_out3, button_1_out);
  and and_132 (and_132_out, decoder_2_out2, decoder_1_out2, button_1_out);
  D_Flip_Flop d_ff_68 (.clk(and_132_out), .D(register_1_q[7]), .Q(d_ff_68_q));  // open: Qn, preset, en, reset
  and and_133 (and_13_out[4], d_ff_65_q, decoder_1_out0, decoder_2_out2);
  and and_134 (and_13_out[4], d_ff_66_q, decoder_1_out1, decoder_2_out2);
  and and_135 (and_15_out[4], d_ff_67_q, decoder_1_out3, decoder_2_out2);
  and and_136 (and_15_out[4], d_ff_68_q, decoder_1_out2, decoder_2_out2);
  and and_137 (and_137_out, decoder_2_out2, decoder_1_out0, button_1_out);
  and and_138 (and_138_out, decoder_2_out2, decoder_1_out1, button_1_out);
  and and_139 (and_139_out, decoder_2_out2, decoder_1_out3, button_1_out);
  and and_140 (and_140_out, decoder_2_out2, decoder_1_out2, button_1_out);
  D_Flip_Flop d_ff_69 (.clk(and_137_out), .D(register_1_q[6]), .Q(d_ff_69_q));  // open: Qn, preset, en, reset
  and and_141 (and_13_out[1], d_ff_69_q, decoder_1_out0, decoder_2_out2);
  D_Flip_Flop d_ff_70 (.clk(and_138_out), .D(register_1_q[6]), .Q(d_ff_70_q));  // open: Qn, preset, en, reset
  and and_142 (and_13_out[1], d_ff_70_q, decoder_1_out1, decoder_2_out2);
  D_Flip_Flop d_ff_71 (.clk(and_139_out), .D(register_1_q[6]), .Q(d_ff_71_q));  // open: Qn, preset, en, reset
  and and_143 (and_15_out[1], d_ff_71_q, decoder_1_out3, decoder_2_out2);
  D_Flip_Flop d_ff_72 (.clk(and_140_out), .D(register_1_q[6]), .Q(d_ff_72_q));  // open: Qn, preset, en, reset
  and and_144 (and_15_out[1], d_ff_72_q, decoder_1_out2, decoder_2_out2);
  and and_145 (and_145_out, decoder_2_out2, decoder_1_out0, button_1_out);
  and and_146 (and_146_out, decoder_2_out2, decoder_1_out1, button_1_out);
  and and_147 (and_147_out, decoder_2_out2, decoder_1_out3, button_1_out);
  and and_148 (and_148_out, decoder_2_out2, decoder_1_out2, button_1_out);
  D_Flip_Flop d_ff_73 (.clk(and_145_out), .D(register_1_q[5]), .Q(d_ff_73_q));  // open: Qn, preset, en, reset
  D_Flip_Flop d_ff_74 (.clk(and_146_out), .D(register_1_q[5]), .Q(d_ff_74_q));  // open: Qn, preset, en, reset
  D_Flip_Flop d_ff_75 (.clk(and_147_out), .D(register_1_q[5]), .Q(d_ff_75_q));  // open: Qn, preset, en, reset
  D_Flip_Flop d_ff_76 (.clk(and_148_out), .D(register_1_q[5]), .Q(d_ff_76_q));  // open: Qn, preset, en, reset
  and and_149 (and_13_out[2], d_ff_73_q, decoder_1_out0, decoder_2_out2);
  and and_150 (and_13_out[2], d_ff_74_q, decoder_1_out1, decoder_2_out2);
  and and_151 (and_15_out[2], d_ff_75_q, decoder_1_out3, decoder_2_out2);
  and and_152 (and_15_out[2], d_ff_76_q, decoder_1_out2, decoder_2_out2);
  and and_153 (and_153_out, decoder_2_out2, decoder_1_out0, button_1_out);
  and and_154 (and_154_out, decoder_2_out2, decoder_1_out1, button_1_out);
  and and_155 (and_155_out, decoder_2_out2, decoder_1_out3, button_1_out);
  and and_156 (and_156_out, decoder_2_out2, decoder_1_out2, button_1_out);
  D_Flip_Flop d_ff_77 (.clk(and_153_out), .D(register_1_q[4]), .Q(d_ff_77_q));  // open: Qn, preset, en, reset
  D_Flip_Flop d_ff_78 (.clk(and_154_out), .D(register_1_q[4]), .Q(d_ff_78_q));  // open: Qn, preset, en, reset
  D_Flip_Flop d_ff_79 (.clk(and_155_out), .D(register_1_q[4]), .Q(d_ff_79_q));  // open: Qn, preset, en, reset
  D_Flip_Flop d_ff_80 (.clk(and_156_out), .D(register_1_q[4]), .Q(d_ff_80_q));  // open: Qn, preset, en, reset
  and and_157 (and_13_out[3], d_ff_77_q, decoder_1_out0, decoder_2_out2);
  and and_158 (and_13_out[3], d_ff_78_q, decoder_1_out1, decoder_2_out2);
  and and_159 (and_15_out[3], d_ff_79_q, decoder_1_out3, decoder_2_out2);
  and and_160 (and_15_out[3], d_ff_80_q, decoder_1_out2, decoder_2_out2);
  and and_161 (and_161_out, decoder_2_out2, decoder_1_out0, button_1_out);
  and and_162 (and_162_out, decoder_2_out2, decoder_1_out1, button_1_out);
  and and_163 (and_163_out, decoder_2_out2, decoder_1_out3, button_1_out);
  and and_164 (and_164_out, decoder_2_out2, decoder_1_out2, button_1_out);
  D_Flip_Flop d_ff_81 (.clk(and_161_out), .D(register_1_q[3]), .Q(d_ff_81_q));  // open: Qn, preset, en, reset
  D_Flip_Flop d_ff_82 (.clk(and_162_out), .D(register_1_q[3]), .Q(d_ff_82_q));  // open: Qn, preset, en, reset
  D_Flip_Flop d_ff_83 (.clk(and_163_out), .D(register_1_q[3]), .Q(d_ff_83_q));  // open: Qn, preset, en, reset
  D_Flip_Flop d_ff_84 (.clk(and_164_out), .D(register_1_q[3]), .Q(d_ff_84_q));  // open: Qn, preset, en, reset
  and and_165 (and_13_out[4], d_ff_81_q, decoder_1_out0, decoder_2_out2);
  and and_166 (and_13_out[4], d_ff_82_q, decoder_1_out1, decoder_2_out2);
  and and_167 (and_15_out[4], d_ff_83_q, decoder_1_out3, decoder_2_out2);
  and and_168 (and_15_out[4], d_ff_84_q, decoder_1_out2, decoder_2_out2);
  and and_169 (and_169_out, decoder_2_out2, decoder_1_out0, button_1_out);
  and and_170 (and_170_out, decoder_2_out2, decoder_1_out1, button_1_out);
  and and_171 (and_171_out, decoder_2_out2, decoder_1_out3, button_1_out);
  and and_172 (and_172_out, decoder_2_out2, decoder_1_out2, button_1_out);
  D_Flip_Flop d_ff_85 (.clk(and_169_out), .D(register_1_q[2]), .Q(d_ff_85_q));  // open: Qn, preset, en, reset
  D_Flip_Flop d_ff_86 (.clk(and_170_out), .D(register_1_q[2]), .Q(d_ff_86_q));  // open: Qn, preset, en, reset
  D_Flip_Flop d_ff_87 (.clk(and_171_out), .D(register_1_q[2]), .Q(d_ff_87_q));  // open: Qn, preset, en, reset
  D_Flip_Flop d_ff_88 (.clk(and_172_out), .D(register_1_q[2]), .Q(d_ff_88_q));  // open: Qn, preset, en, reset
  and and_173 (and_13_out[5], d_ff_85_q, decoder_1_out0, decoder_2_out2);
  and and_174 (and_13_out[5], d_ff_86_q, decoder_1_out1, decoder_2_out2);
  and and_175 (and_15_out[5], d_ff_87_q, decoder_1_out3, decoder_2_out2);
  and and_176 (and_15_out[5], d_ff_88_q, decoder_1_out2, decoder_2_out2);
  and and_177 (and_177_out, decoder_2_out2, decoder_1_out0, button_1_out);
  and and_178 (and_178_out, decoder_2_out2, decoder_1_out1, button_1_out);
  and and_179 (and_179_out, decoder_2_out2, decoder_1_out3, button_1_out);
  and and_180 (and_180_out, decoder_2_out2, decoder_1_out2, button_1_out);
  D_Flip_Flop d_ff_89 (.clk(and_177_out), .D(register_1_q[1]), .Q(d_ff_89_q));  // open: Qn, preset, en, reset
  D_Flip_Flop d_ff_90 (.clk(and_178_out), .D(register_1_q[1]), .Q(d_ff_90_q));  // open: Qn, preset, en, reset
  D_Flip_Flop d_ff_91 (.clk(and_179_out), .D(register_1_q[1]), .Q(d_ff_91_q));  // open: Qn, preset, en, reset
  D_Flip_Flop d_ff_92 (.clk(and_180_out), .D(register_1_q[1]), .Q(d_ff_92_q));  // open: Qn, preset, en, reset
  and and_181 (and_13_out[6], d_ff_89_q, decoder_1_out0, decoder_2_out2);
  and and_182 (and_13_out[6], d_ff_90_q, decoder_1_out1, decoder_2_out2);
  and and_183 (and_15_out[6], d_ff_91_q, decoder_1_out3, decoder_2_out2);
  and and_184 (and_15_out[6], d_ff_92_q, decoder_1_out2, decoder_2_out2);
  and and_185 (and_185_out, decoder_2_out2, decoder_1_out0, button_1_out);
  and and_186 (and_186_out, decoder_2_out2, decoder_1_out1, button_1_out);
  and and_187 (and_187_out, decoder_2_out2, decoder_1_out3, button_1_out);
  and and_188 (and_188_out, decoder_2_out2, decoder_1_out2, button_1_out);
  D_Flip_Flop d_ff_93 (.clk(and_185_out), .D(register_1_q[0]), .Q(d_ff_93_q));  // open: Qn, preset, en, reset
  D_Flip_Flop d_ff_94 (.clk(and_186_out), .D(register_1_q[0]), .Q(d_ff_94_q));  // open: Qn, preset, en, reset
  D_Flip_Flop d_ff_95 (.clk(and_187_out), .D(register_1_q[0]), .Q(d_ff_95_q));  // open: Qn, preset, en, reset
  D_Flip_Flop d_ff_96 (.clk(and_188_out), .D(register_1_q[0]), .Q(d_ff_96_q));  // open: Qn, preset, en, reset
  and and_189 (and_13_out[7], d_ff_93_q, decoder_1_out0, decoder_2_out2);
  and and_190 (and_13_out[7], d_ff_94_q, decoder_1_out1, decoder_2_out2);
  and and_191 (and_15_out[7], d_ff_95_q, decoder_1_out3, decoder_2_out2);
  and and_192 (and_15_out[7], d_ff_96_q, decoder_1_out2, decoder_2_out2);
  and and_193 (and_193_out, decoder_2_out3, decoder_1_out0, button_1_out);
  and and_194 (and_194_out, decoder_2_out3, decoder_1_out1, button_1_out);
  and and_195 (and_195_out, decoder_2_out3, decoder_1_out3, button_1_out);
  and and_196 (and_196_out, decoder_2_out3, decoder_1_out2, button_1_out);
  D_Flip_Flop d_ff_97 (.clk(and_193_out), .D(register_1_q[7]), .Q(d_ff_97_q));  // open: Qn, preset, en, reset
  and and_197 (and_13_out[4], d_ff_97_q, decoder_1_out0, decoder_2_out3);
  D_Flip_Flop d_ff_98 (.clk(and_194_out), .D(register_1_q[7]), .Q(d_ff_98_q));  // open: Qn, preset, en, reset
  and and_198 (and_13_out[4], d_ff_98_q, decoder_1_out1, decoder_2_out3);
  D_Flip_Flop d_ff_99 (.clk(and_195_out), .D(register_1_q[7]), .Q(d_ff_99_q));  // open: Qn, preset, en, reset
  and and_199 (and_15_out[4], d_ff_99_q, decoder_1_out3, decoder_2_out3);
  D_Flip_Flop d_ff_100 (.clk(and_196_out), .D(register_1_q[7]), .Q(d_ff_100_q));  // open: Qn, preset, en, reset
  and and_200 (and_15_out[4], d_ff_100_q, decoder_1_out2, decoder_2_out3);
  and and_201 (and_201_out, decoder_2_out3, decoder_1_out0, button_1_out);
  and and_202 (and_202_out, decoder_2_out3, decoder_1_out1, button_1_out);
  and and_203 (and_203_out, decoder_2_out3, decoder_1_out3, button_1_out);
  and and_204 (and_204_out, decoder_2_out3, decoder_1_out2, button_1_out);
  D_Flip_Flop d_ff_101 (.clk(and_201_out), .D(register_1_q[6]), .Q(d_ff_101_q));  // open: Qn, preset, en, reset
  D_Flip_Flop d_ff_102 (.clk(and_202_out), .D(register_1_q[6]), .Q(d_ff_102_q));  // open: Qn, preset, en, reset
  D_Flip_Flop d_ff_103 (.clk(and_203_out), .D(register_1_q[6]), .Q(d_ff_103_q));  // open: Qn, preset, en, reset
  D_Flip_Flop d_ff_104 (.clk(and_204_out), .D(register_1_q[6]), .Q(d_ff_104_q));  // open: Qn, preset, en, reset
  and and_205 (and_13_out[1], d_ff_101_q, decoder_1_out0, decoder_2_out3);
  and and_206 (and_13_out[1], d_ff_102_q, decoder_1_out1, decoder_2_out3);
  and and_207 (and_15_out[1], d_ff_103_q, decoder_1_out3, decoder_2_out3);
  and and_208 (and_15_out[1], d_ff_104_q, decoder_1_out2, decoder_2_out3);
  and and_209 (and_209_out, decoder_2_out3, decoder_1_out0, button_1_out);
  and and_210 (and_210_out, decoder_2_out3, decoder_1_out1, button_1_out);
  and and_211 (and_211_out, decoder_2_out3, decoder_1_out3, button_1_out);
  and and_212 (and_212_out, decoder_2_out3, decoder_1_out2, button_1_out);
  D_Flip_Flop d_ff_105 (.clk(and_209_out), .D(register_1_q[5]), .Q(d_ff_105_q));  // open: Qn, preset, en, reset
  D_Flip_Flop d_ff_106 (.clk(and_210_out), .D(register_1_q[5]), .Q(d_ff_106_q));  // open: Qn, preset, en, reset
  D_Flip_Flop d_ff_107 (.clk(and_211_out), .D(register_1_q[5]), .Q(d_ff_107_q));  // open: Qn, preset, en, reset
  D_Flip_Flop d_ff_108 (.clk(and_212_out), .D(register_1_q[5]), .Q(d_ff_108_q));  // open: Qn, preset, en, reset
  and and_213 (and_13_out[2], d_ff_105_q, decoder_1_out0, decoder_2_out3);
  and and_214 (and_13_out[2], d_ff_106_q, decoder_1_out1, decoder_2_out3);
  and and_215 (and_15_out[2], d_ff_107_q, decoder_1_out3, decoder_2_out3);
  and and_216 (and_15_out[2], d_ff_108_q, decoder_1_out2, decoder_2_out3);
  and and_217 (and_217_out, decoder_2_out3, decoder_1_out0, button_1_out);
  and and_218 (and_218_out, decoder_2_out3, decoder_1_out1, button_1_out);
  and and_219 (and_219_out, decoder_2_out3, decoder_1_out3, button_1_out);
  and and_220 (and_220_out, decoder_2_out3, decoder_1_out2, button_1_out);
  D_Flip_Flop d_ff_109 (.clk(and_217_out), .D(register_1_q[4]), .Q(d_ff_109_q));  // open: Qn, preset, en, reset
  D_Flip_Flop d_ff_110 (.clk(and_218_out), .D(register_1_q[4]), .Q(d_ff_110_q));  // open: Qn, preset, en, reset
  D_Flip_Flop d_ff_111 (.clk(and_219_out), .D(register_1_q[4]), .Q(d_ff_111_q));  // open: Qn, preset, en, reset
  D_Flip_Flop d_ff_112 (.clk(and_220_out), .D(register_1_q[4]), .Q(d_ff_112_q));  // open: Qn, preset, en, reset
  and and_221 (and_13_out[3], d_ff_109_q, decoder_1_out0, decoder_2_out3);
  and and_222 (and_13_out[3], d_ff_110_q, decoder_1_out1, decoder_2_out3);
  and and_223 (and_15_out[3], d_ff_111_q, decoder_1_out3, decoder_2_out3);
  and and_224 (and_15_out[3], d_ff_112_q, decoder_1_out2, decoder_2_out3);
  and and_225 (and_225_out, decoder_2_out3, decoder_1_out0, button_1_out);
  and and_226 (and_226_out, decoder_2_out3, decoder_1_out1, button_1_out);
  and and_227 (and_227_out, decoder_2_out3, decoder_1_out3, button_1_out);
  and and_228 (and_228_out, decoder_2_out3, decoder_1_out2, button_1_out);
  D_Flip_Flop d_ff_113 (.clk(and_225_out), .D(register_1_q[3]), .Q(d_ff_113_q));  // open: Qn, preset, en, reset
  D_Flip_Flop d_ff_114 (.clk(and_226_out), .D(register_1_q[3]), .Q(d_ff_114_q));  // open: Qn, preset, en, reset
  D_Flip_Flop d_ff_115 (.clk(and_227_out), .D(register_1_q[3]), .Q(d_ff_115_q));  // open: Qn, preset, en, reset
  D_Flip_Flop d_ff_116 (.clk(and_228_out), .D(register_1_q[3]), .Q(d_ff_116_q));  // open: Qn, preset, en, reset
  and and_229 (and_13_out[4], d_ff_113_q, decoder_1_out0, decoder_2_out3);
  and and_230 (and_13_out[4], d_ff_114_q, decoder_1_out1, decoder_2_out3);
  and and_231 (and_15_out[4], d_ff_115_q, decoder_1_out3, decoder_2_out3);
  and and_232 (and_15_out[4], d_ff_116_q, decoder_1_out2, decoder_2_out3);
  and and_233 (and_233_out, decoder_2_out3, decoder_1_out0, button_1_out);
  and and_234 (and_234_out, decoder_2_out3, decoder_1_out1, button_1_out);
  and and_235 (and_235_out, decoder_2_out3, decoder_1_out3, button_1_out);
  and and_236 (and_236_out, decoder_2_out3, decoder_1_out2, button_1_out);
  D_Flip_Flop d_ff_117 (.clk(and_233_out), .D(register_1_q[2]), .Q(d_ff_117_q));  // open: Qn, preset, en, reset
  D_Flip_Flop d_ff_118 (.clk(and_234_out), .D(register_1_q[2]), .Q(d_ff_118_q));  // open: Qn, preset, en, reset
  D_Flip_Flop d_ff_119 (.clk(and_235_out), .D(register_1_q[2]), .Q(d_ff_119_q));  // open: Qn, preset, en, reset
  D_Flip_Flop d_ff_120 (.clk(and_236_out), .D(register_1_q[2]), .Q(d_ff_120_q));  // open: Qn, preset, en, reset
  and and_237 (and_13_out[5], d_ff_117_q, decoder_1_out0, decoder_2_out3);
  and and_238 (and_13_out[5], d_ff_118_q, decoder_1_out1, decoder_2_out3);
  and and_239 (and_15_out[5], d_ff_119_q, decoder_1_out3, decoder_2_out3);
  and and_240 (and_15_out[5], d_ff_120_q, decoder_1_out2, decoder_2_out3);
  and and_241 (and_241_out, decoder_2_out3, decoder_1_out0, button_1_out);
  and and_242 (and_242_out, decoder_2_out3, decoder_1_out1, button_1_out);
  and and_243 (and_243_out, decoder_2_out3, decoder_1_out3, button_1_out);
  and and_244 (and_244_out, decoder_2_out3, decoder_1_out2, button_1_out);
  D_Flip_Flop d_ff_121 (.clk(and_241_out), .D(register_1_q[1]), .Q(d_ff_121_q));  // open: Qn, preset, en, reset
  D_Flip_Flop d_ff_122 (.clk(and_242_out), .D(register_1_q[1]), .Q(d_ff_122_q));  // open: Qn, preset, en, reset
  D_Flip_Flop d_ff_123 (.clk(and_243_out), .D(register_1_q[1]), .Q(d_ff_123_q));  // open: Qn, preset, en, reset
  D_Flip_Flop d_ff_124 (.clk(and_244_out), .D(register_1_q[1]), .Q(d_ff_124_q));  // open: Qn, preset, en, reset
  and and_245 (and_13_out[6], d_ff_121_q, decoder_1_out0, decoder_2_out3);
  and and_246 (and_13_out[6], d_ff_122_q, decoder_1_out1, decoder_2_out3);
  and and_247 (and_15_out[6], d_ff_123_q, decoder_1_out3, decoder_2_out3);
  and and_248 (and_15_out[6], d_ff_124_q, decoder_1_out2, decoder_2_out3);
  D_Flip_Flop d_ff_125 (.clk(and_249_out), .D(register_1_q[0]), .Q(d_ff_125_q));  // open: Qn, preset, en, reset
  and and_249 (and_249_out, decoder_2_out3, decoder_1_out0, button_1_out);
  and and_250 (and_250_out, decoder_2_out3, decoder_1_out1, button_1_out);
  D_Flip_Flop d_ff_126 (.clk(and_250_out), .D(register_1_q[0]), .Q(d_ff_126_q));  // open: Qn, preset, en, reset
  D_Flip_Flop d_ff_127 (.clk(and_251_out), .D(register_1_q[0]), .Q(d_ff_127_q));  // open: Qn, preset, en, reset
  and and_251 (and_251_out, decoder_2_out3, decoder_1_out3, button_1_out);
  D_Flip_Flop d_ff_128 (.clk(and_252_out), .D(register_1_q[0]), .Q(d_ff_128_q));  // open: Qn, preset, en, reset
  and and_252 (and_252_out, decoder_2_out3, decoder_1_out2, button_1_out);
  and and_253 (and_13_out[7], d_ff_125_q, decoder_1_out0, decoder_2_out3);
  and and_254 (and_13_out[7], d_ff_126_q, decoder_1_out1, decoder_2_out3);
  and and_255 (and_15_out[7], d_ff_127_q, decoder_1_out3, decoder_2_out3);
  and and_256 (and_15_out[7], d_ff_128_q, decoder_1_out2, decoder_2_out3);

  // Notes on the sheet:
  //   and_5 drives only 0 and floats otherwise
  //   and_29 drives only 1 and floats otherwise
  //   and_30 drives only 1 and floats otherwise
  //   and_93 drives only 1 and floats otherwise
  //   and_94 drives only 1 and floats otherwise
  //   and_157 drives only 1 and floats otherwise
  //   and_158 drives only 1 and floats otherwise
  //   and_221 drives only 1 and floats otherwise
  //   and_222 drives only 1 and floats otherwise
endmodule
