// Logisim project instruction_execution.circ as structural Verilog: 1 circuit, main circuit main
module main (
  output [15:0] out_1,
  output [3:0] Reg_Addr
);

  wire and_4_out, button_1_out, d_ff_1_q, d_ff_2_q, decoder_1_out0, decoder_1_out1, decoder_1_out2,
       decoder_1_out3, decoder_1_out4, decoder_1_out5, decoder_1_out6, decoder_1_out7, decoder_1_out8,
       decoder_1_out9, decoder_1_out10, decoder_1_out11, decoder_1_out12, decoder_1_out13, decoder_1_out14,
       decoder_1_out15, decoder_2_out0, decoder_2_out1, decoder_2_out2, decoder_2_out3, decoder_2_out4,
       decoder_2_out5, decoder_2_out6, decoder_2_out7, decoder_2_out8, decoder_2_out9, decoder_2_out10,
       decoder_2_out11, decoder_2_out12, decoder_2_out13, decoder_2_out14, decoder_2_out15,
       demultiplexer_1_out0, demultiplexer_1_out1, j_k_ff_1_q, Main_Clock_out, not_1_out, not_2_out,
       not_3_out, not_4_out, not_5_out, not_6_out, not_7_out, not_8_out, not_9_out, or_1_out,
       pull_resistor_1_node, undriven, undriven_2, xor_1_out;
  wire [7:0] counter_1_q, counter_2_q, counter_3_q, counter_4_q, counter_5_q, counter_6_q, counter_7_q,
       counter_8_q, multiplexer_1_out, PRogram_Counter_q, ram_1_data;

  Button button_1 (.out(button_1_out));
  RAM ram_1 (.addr(PRogram_Counter_q), .data(ram_1_data), .sel(1'b1), .clk(button_1_out));  // open: ld, clr
  Shift_Register #(.length(1)) shift_register_1 (
    .shift(undriven), .in(ram_1_data[0]), .clk(demultiplexer_1_out0), .out(out_1[15]));  // open: load, clr, d0, q0
  Shift_Register #(.length(1)) shift_register_2 (
    .shift(undriven), .in(ram_1_data[1]), .clk(demultiplexer_1_out0), .out(out_1[14]));  // open: load, clr, d0, q0
  Shift_Register #(.length(1)) shift_register_3 (
    .shift(undriven), .in(ram_1_data[2]), .clk(demultiplexer_1_out0), .out(out_1[13]));  // open: load, clr, d0, q0
  Shift_Register #(.length(1)) shift_register_4 (
    .shift(undriven), .in(ram_1_data[3]), .clk(demultiplexer_1_out0), .out(out_1[12]));  // open: load, clr, d0, q0
  Shift_Register #(.length(1)) shift_register_5 (
    .shift(undriven), .in(ram_1_data[4]), .clk(demultiplexer_1_out0), .out(out_1[11]));  // open: load, clr, d0, q0
  Shift_Register #(.length(1)) shift_register_6 (
    .shift(undriven), .in(ram_1_data[5]), .clk(demultiplexer_1_out0), .out(out_1[10]));  // open: load, clr, d0, q0
  Shift_Register #(.length(1)) shift_register_7 (
    .shift(undriven), .in(ram_1_data[6]), .clk(demultiplexer_1_out0), .out(out_1[9]));  // open: load, clr, d0, q0
  Shift_Register #(.length(1)) shift_register_8 (
    .shift(undriven), .in(ram_1_data[7]), .clk(demultiplexer_1_out0), .out(out_1[8]));  // open: load, clr, d0, q0
  xor xor_1 (xor_1_out, d_ff_1_q, 1'b1);
  D_Flip_Flop d_ff_1 (.clk(demultiplexer_1_out0), .D(xor_1_out), .Q(d_ff_1_q));  // open: Qn, preset, en, reset
  Shift_Register #(.length(1)) shift_register_9 (
    .shift(undriven_2), .in(out_1[15]), .clk(demultiplexer_1_out0), .out(out_1[7]));  // open: load, clr, d0, q0
  Shift_Register #(.length(1)) shift_register_10 (
    .shift(undriven_2), .in(out_1[14]), .clk(demultiplexer_1_out0), .out(out_1[6]));  // open: load, clr, d0, q0
  Shift_Register #(.length(1)) shift_register_11 (
    .shift(undriven_2), .in(out_1[13]), .clk(demultiplexer_1_out0), .out(out_1[5]));  // open: load, clr, d0, q0
  Shift_Register #(.length(1)) shift_register_12 (
    .shift(undriven_2), .in(out_1[12]), .clk(demultiplexer_1_out0), .out(out_1[4]));  // open: load, clr, d0, q0
  Shift_Register #(.length(1)) shift_register_13 (
    .shift(undriven_2), .in(out_1[11]), .clk(demultiplexer_1_out0), .out(out_1[3]));  // open: load, clr, d0, q0
  Shift_Register #(.length(1)) shift_register_14 (
    .shift(undriven_2), .in(out_1[10]), .clk(demultiplexer_1_out0), .out(out_1[2]));  // open: load, clr, d0, q0
  Shift_Register #(.length(1)) shift_register_15 (
    .shift(undriven_2), .in(out_1[9]), .clk(demultiplexer_1_out0), .out(out_1[1]));  // open: load, clr, d0, q0
  Shift_Register #(.length(1)) shift_register_16 (
    .shift(undriven_2), .in(out_1[8]), .clk(demultiplexer_1_out0), .out(out_1[0]));  // open: load, clr, d0, q0
  D_Flip_Flop d_ff_2 (.clk(demultiplexer_1_out0), .D(d_ff_1_q), .Q(d_ff_2_q));  // open: Qn, preset, en, reset
  Pull_Resistor pull_resistor_1 (.node(pull_resistor_1_node));
  Decoder #(.select(4), .disabled(0)) decoder_1 (
    .out0(decoder_1_out0), .out1(decoder_1_out1), .out2(decoder_1_out2), .out3(decoder_1_out3),
    .out4(decoder_1_out4), .out5(decoder_1_out5), .out6(decoder_1_out6), .out7(decoder_1_out7),
    .out8(decoder_1_out8), .out9(decoder_1_out9), .out10(decoder_1_out10), .out11(decoder_1_out11),
    .out12(decoder_1_out12), .out13(decoder_1_out13), .out14(decoder_1_out14), .out15(decoder_1_out15),
    .sel(out_1[3:0]), .en(d_ff_2_q));
  Clock Main_Clock (.out(Main_Clock_out));
  Demultiplexer demultiplexer_1 (
    .out0(demultiplexer_1_out0), .out1(demultiplexer_1_out1), .in(Main_Clock_out), .sel(j_k_ff_1_q));  // open: en
  J_K_Flip_Flop #(.trigger("falling")) j_k_ff_1 (
    .J(d_ff_2_q), .clk(Main_Clock_out), .K(pull_resistor_1_node), .Q(j_k_ff_1_q));  // open: Qn, preset, en, reset
  and and_1 (pull_resistor_1_node, demultiplexer_1_out1, decoder_1_out0);
  and and_2 (pull_resistor_1_node, decoder_1_out1, demultiplexer_1_out1);
  and and_3 (pull_resistor_1_node, decoder_1_out2, demultiplexer_1_out1);
  buf buffer_1 (pull_resistor_1_node, and_4_out);
  and and_4 (and_4_out, decoder_1_out3, demultiplexer_1_out1);
  Pull_Resistor pull_resistor_2 (.node(and_4_out));
  or or_1 (or_1_out, demultiplexer_1_out0, and_4_out);
  Decoder #(.select(4), .disabled(0)) decoder_2 (
    .out0(decoder_2_out0), .out1(decoder_2_out1), .out2(decoder_2_out2), .out3(decoder_2_out3),
    .out4(decoder_2_out4), .out5(decoder_2_out5), .out6(decoder_2_out6), .out7(decoder_2_out7),
    .out8(decoder_2_out8), .out9(decoder_2_out9), .out10(decoder_2_out10), .out11(decoder_2_out11),
    .out12(decoder_2_out12), .out13(decoder_2_out13), .out14(decoder_2_out14), .out15(decoder_2_out15),
    .sel(out_1[7:4]), .en(pull_resistor_1_node));
  Pull_Resistor pull_resistor_3 (.node(decoder_1_out3));
  not not_1 (not_1_out, decoder_1_out1);
  not not_2 (not_2_out, decoder_1_out1);
  not not_3 (not_3_out, decoder_1_out1);
  not not_4 (not_4_out, decoder_1_out1);
  not not_5 (not_5_out, decoder_1_out1);
  not not_6 (not_6_out, decoder_1_out1);
  not not_7 (not_7_out, decoder_1_out1);
  not not_8 (not_8_out, decoder_1_out1);
  Counter #(.trigger("falling")) PRogram_Counter (
    .load(decoder_1_out3), .D(out_1[15:8]), .count(not_9_out), .Q(PRogram_Counter_q), .clk(or_1_out));  // open: carry, clr
  not not_9 (not_9_out, decoder_1_out3);
  Counter counter_1 (
    .load(decoder_1_out1), .D(out_1[15:8]), .count(not_1_out), .Q(counter_1_q), .clk(decoder_2_out1));  // open: carry, clr
  Counter counter_2 (
    .load(decoder_1_out1), .D(out_1[15:8]), .count(not_2_out), .Q(counter_2_q), .clk(decoder_2_out2));  // open: carry, clr
  Counter counter_3 (
    .load(decoder_1_out1), .D(out_1[15:8]), .count(not_3_out), .Q(counter_3_q), .clk(decoder_2_out3));  // open: carry, clr
  Counter counter_4 (
    .load(decoder_1_out1), .D(out_1[15:8]), .count(not_4_out), .Q(counter_4_q), .clk(decoder_2_out4));  // open: carry, clr
  Counter counter_5 (
    .load(decoder_1_out1), .D(out_1[15:8]), .count(not_5_out), .Q(counter_5_q), .clk(decoder_2_out5));  // open: carry, clr
  Counter counter_6 (
    .load(decoder_1_out1), .D(out_1[15:8]), .count(not_6_out), .Q(counter_6_q), .clk(decoder_2_out5));  // open: carry, clr
  Counter counter_7 (
    .load(decoder_1_out1), .D(out_1[15:8]), .count(not_7_out), .Q(counter_7_q), .clk(decoder_2_out6));  // open: carry, clr
  Counter counter_8 (
    .load(decoder_1_out1), .D(out_1[15:8]), .count(not_8_out), .Q(counter_8_q), .clk(decoder_2_out7));  // open: carry, clr
  Multiplexer #(.select(4), .width(8)) multiplexer_1 (
    .in0(PRogram_Counter_q), .in1(counter_1_q), .in2(counter_2_q), .in3(counter_3_q), .in4(counter_4_q),
    .in5(counter_5_q), .in6(counter_6_q), .in7(counter_7_q), .in8(counter_8_q), .out(multiplexer_1_out),
    .sel(out_1[7:4]));  // open: in9, in10, in11, in12, in13, in14, in15, en

  assign Reg_Addr = out_1[7:4];

  // Notes on the sheet:
  //   Instruction Fetching
  //   Delay 2 cycles 
  //   Instruction Ready
  //   Data
  //   NC. 0xF = HALT
  //   Instruction End
  //   Op Code
  //   Instruction Clock
  //   NOP
  //   and_1 drives only 1 and floats otherwise
  //   LOADI
  //   and_2 drives only 1 and floats otherwise
  //   INC
  //   and_3 drives only 1 and floats otherwise
  //   buffer_1 drives only 1 and floats otherwise
  //   BRANCH
  //   and_4 drives only 1 and floats otherwise
  //   Read Data
  //   PC CLK
  //   Write/Inc
  //   Write Data
  //   Write CLK
endmodule
